// Logisim project progetto.circ as structural Verilog: 1 circuit, main circuit main
module main (
);

  wire _0_out, _1_out, _2_out, _3_out, _4_out, _5_out, _6_out, _7_out, _8_out, _9_out, annulla_out,
       azzera_out, button_2_out, button_out, canc_out, clock_1_out, load_out, m_calcolatore_1_of,
       m_selection_displayer_1_out_2, m_selection_displayer_1_out_3, m_selection_displayer_1_out_4,
       m_ui_1_azzera_2, m_ui_1_back_2, m_ui_1_cancella_2, m_ui_1_click, m_ui_1_load_2, m_ui_1_ok_2,
       m_ui_1_reset_2, m_ui_1_save_2, ok_out, operation_out, reset_out, save_out;
  wire [1:0] op_code, select;
  wire [2:0] m_op_code_displayer_1_out_2, m_op_code_displayer_1_out_3, m_op_code_displayer_1_out_4;
  wire [3:0] m_input_memory_1_q, m_input_memory_1_q_saved, m_input_memory_1_x, m_input_memory_1_x_2,
       m_input_memory_1_x_2_saved, m_input_memory_1_x_saved, m_ui_1_data;
  wire [4:0] m_calcolatore_1_x, m_calcolatore_1_y;
  wire [31:0] m_drawer_1_out_9, m_drawer_1_out_10, m_drawer_1_out_11, m_drawer_1_out_12, m_drawer_1_out_13,
       m_drawer_1_out_14, m_drawer_1_out_15, m_drawer_1_out_16, m_drawer_1_out_17, m_drawer_1_out_18,
       m_drawer_1_out_19, m_drawer_1_out_20, m_drawer_1_out_21, m_drawer_1_out_22, m_drawer_1_out_23,
       m_drawer_1_out_24, m_drawer_1_out_25, m_drawer_1_out_26, m_drawer_1_out_27, m_drawer_1_out_28,
       m_drawer_1_out_29, m_drawer_1_out_30, m_drawer_1_out_31, m_drawer_1_out_32, m_drawer_1_out_33,
       m_drawer_1_out_34, m_drawer_1_out_35, m_drawer_1_out_36, m_drawer_1_out_37, m_drawer_1_out_38,
       m_drawer_1_out_39, m_drawer_1_out_40;

  Button _7 (.out(_7_out));
  Button _4 (.out(_4_out));
  Button _1 (.out(_1_out));
  Button ok (.out(ok_out));
  Button reset (.out(reset_out));
  Button _9 (.out(_9_out));
  Button _8 (.out(_8_out));
  Button _6 (.out(_6_out));
  Button _5 (.out(_5_out));
  Button _3 (.out(_3_out));
  Button _2 (.out(_2_out));
  Button _0 (.out(_0_out));
  Button button (.out(button_out));
  Button button_2 (.out(button_2_out));
  Button azzera (.out(azzera_out));
  Button annulla (.out(annulla_out));
  Hex_Digit_Display hex_digit_display_1 (.value(m_input_memory_1_x_2_saved));  // open: dp
  DotMatrix #(.matrixcols(3), .matrixrows(3)) dotmatrix_1 (
    .col0(m_op_code_displayer_1_out_2), .col1(m_op_code_displayer_1_out_3), .col2(m_op_code_displayer_1_out_4));
  m_op_code_displayer m_op_code_displayer_1 (
    .op_code(op_code), .out_2(m_op_code_displayer_1_out_2), .out_3(m_op_code_displayer_1_out_3),
    .out_4(m_op_code_displayer_1_out_4));
  m_ui m_ui_1 (
    ._9(_9_out), ._8(_8_out), ._7(_7_out), ._6(_6_out), ._5(_5_out), ._4(_4_out), ._3(_3_out), ._2(_2_out),
    ._1(_1_out), ._0(_0_out), .reset(reset_out), .azzera(azzera_out), .back(annulla_out), .ok(ok_out),
    .right(button_out), .left(button_2_out), .save(save_out), .load(load_out), .cancella(canc_out),
    .op(operation_out), .data(m_ui_1_data), .click(m_ui_1_click), .reset_2(m_ui_1_reset_2),
    .azzera_2(m_ui_1_azzera_2), .back_2(m_ui_1_back_2), .ok_2(m_ui_1_ok_2), .save_2(m_ui_1_save_2),
    .load_2(m_ui_1_load_2), .cancella_2(m_ui_1_cancella_2), .select(select), .op_code(op_code));  // open: right_2, left_2
  Button save (.out(save_out));
  Button load (.out(load_out));
  Button canc (.out(canc_out));
  Hex_Digit_Display hex_digit_display_2 (.value(m_input_memory_1_q_saved));  // open: dp
  Hex_Digit_Display hex_digit_display_3 (.value(m_input_memory_1_x_saved));  // open: dp
  Button operation (.out(operation_out));
  LED led_1 (.in(m_selection_displayer_1_out_3));
  m_selection_displayer m_selection_displayer_1 (
    .select(select), .out_2(m_selection_displayer_1_out_2), .out_3(m_selection_displayer_1_out_3),
    .out_4(m_selection_displayer_1_out_4));
  LED led_2 (.in(m_selection_displayer_1_out_2));
  Hex_Digit_Display hex_digit_display_4 (.value(m_input_memory_1_x));  // open: dp
  Hex_Digit_Display hex_digit_display_5 (.value(m_input_memory_1_x_2));  // open: dp
  m_input_memory m_input_memory_1 (
    .data(m_ui_1_data), .click(m_ui_1_click), .reset(m_ui_1_reset_2), .azzera(m_ui_1_azzera_2),
    .back(m_ui_1_back_2), .ok(m_ui_1_ok_2), .save(m_ui_1_save_2), .load(m_ui_1_load_2),
    .cancella(m_ui_1_cancella_2), .select(select), .x_2(m_input_memory_1_x_2), .x(m_input_memory_1_x),
    .q(m_input_memory_1_q), .x_2_saved(m_input_memory_1_x_2_saved), .x_saved(m_input_memory_1_x_saved),
    .q_saved(m_input_memory_1_q_saved));
  Clock clock_1 (.out(clock_1_out));
  LED led_3 (.in(m_selection_displayer_1_out_4));
  Hex_Digit_Display hex_digit_display_6 (.value(m_input_memory_1_q));  // open: dp
  m_calcolatore m_calcolatore_1 (
    .c_x_2(m_input_memory_1_x_2), .c_x(m_input_memory_1_x), .q(m_input_memory_1_q), .clock(clock_1_out),
    .reset(m_ui_1_reset_2), .y(m_calcolatore_1_y), .of(m_calcolatore_1_of), .x(m_calcolatore_1_x));
  DotMatrix #(.matrixcols(32), .matrixrows(32)) dotmatrix_2 (
    .col0(m_drawer_1_out_9), .col1(m_drawer_1_out_10), .col2(m_drawer_1_out_11), .col3(m_drawer_1_out_12),
    .col4(m_drawer_1_out_13), .col5(m_drawer_1_out_14), .col6(m_drawer_1_out_15), .col7(m_drawer_1_out_16),
    .col8(m_drawer_1_out_17), .col9(m_drawer_1_out_18), .col10(m_drawer_1_out_19), .col11(m_drawer_1_out_20),
    .col12(m_drawer_1_out_21), .col13(m_drawer_1_out_22), .col14(m_drawer_1_out_23),
    .col15(m_drawer_1_out_24), .col16(m_drawer_1_out_25), .col17(m_drawer_1_out_26),
    .col18(m_drawer_1_out_27), .col19(m_drawer_1_out_28), .col20(m_drawer_1_out_29),
    .col21(m_drawer_1_out_30), .col22(m_drawer_1_out_31), .col23(m_drawer_1_out_32),
    .col24(m_drawer_1_out_33), .col25(m_drawer_1_out_34), .col26(m_drawer_1_out_35),
    .col27(m_drawer_1_out_36), .col28(m_drawer_1_out_37), .col29(m_drawer_1_out_38),
    .col30(m_drawer_1_out_39), .col31(m_drawer_1_out_40));
  m_drawer m_drawer_1 (
    .x(m_calcolatore_1_x), .y(m_calcolatore_1_y), .of(m_calcolatore_1_of), .clock(clock_1_out),
    .reset(m_ui_1_reset_2), .save(m_ui_1_save_2), .cancella(m_ui_1_cancella_2), .op_code(op_code),
    .out_9(m_drawer_1_out_9), .out_10(m_drawer_1_out_10), .out_11(m_drawer_1_out_11),
    .out_12(m_drawer_1_out_12), .out_13(m_drawer_1_out_13), .out_14(m_drawer_1_out_14),
    .out_15(m_drawer_1_out_15), .out_16(m_drawer_1_out_16), .out_17(m_drawer_1_out_17),
    .out_18(m_drawer_1_out_18), .out_19(m_drawer_1_out_19), .out_20(m_drawer_1_out_20),
    .out_21(m_drawer_1_out_21), .out_22(m_drawer_1_out_22), .out_23(m_drawer_1_out_23),
    .out_24(m_drawer_1_out_24), .out_25(m_drawer_1_out_25), .out_26(m_drawer_1_out_26),
    .out_27(m_drawer_1_out_27), .out_28(m_drawer_1_out_28), .out_29(m_drawer_1_out_29),
    .out_30(m_drawer_1_out_30), .out_31(m_drawer_1_out_31), .out_32(m_drawer_1_out_32),
    .out_33(m_drawer_1_out_33), .out_34(m_drawer_1_out_34), .out_35(m_drawer_1_out_35),
    .out_36(m_drawer_1_out_36), .out_37(m_drawer_1_out_37), .out_38(m_drawer_1_out_38),
    .out_39(m_drawer_1_out_39), .out_40(m_drawer_1_out_40));

  // Notes on the sheet:
  //   x^2
  //   OP
  //   SALVATO
  //   q
  //   x
  //   ATTUALE
  //   x
  //   x^2
  //   q
endmodule
